// Logisim project HW2.circ as structural Verilog
module exc262 (
  input  x1,
  input  x2,
  input  x3,
  output f
);

  wire not_1_out, not_2_out, not_3_out, or_1_out, or_2_out;

  not not_1 (not_1_out, x1);
  not not_2 (not_2_out, x2);
  not not_3 (not_3_out, x3);
  or or_1 (or_1_out, x1, x2, x3);
  or or_2 (or_2_out, not_1_out, not_2_out, not_3_out);
  and and_1 (f, or_1_out, or_2_out);
endmodule

module exc_262 (
  input  x1,
  input  x2,
  input  x3,
  output f
);

  wire not_1_out, not_2_out, not_3_out, or_1_out, or_2_out;

  not not_1 (not_1_out, x1);
  not not_2 (not_2_out, x2);
  not not_3 (not_3_out, x3);
  or or_1 (or_1_out, x1, x2, x3);
  or or_2 (or_2_out, not_1_out, not_2_out, not_3_out);
  and and_1 (f, or_1_out, or_2_out);
endmodule

module exc_263 (
  input  x1,
  input  x2,
  input  x3,
  output f
);

  wire not_1_out, not_2_out, not_3_out, or_1_out, or_2_out;

  not not_1 (not_1_out, x1);
  not not_2 (not_2_out, x2);
  not not_3 (not_3_out, x3);
  or or_1 (or_1_out, x1, not_2_out, x3);
  or or_2 (or_2_out, not_1_out, not_2_out, not_3_out);
  and and_1 (f, or_1_out, or_2_out);
endmodule

module exc_321 (
  input  b2,
  input  b1,
  input  b0,
  output s1,
  output s0
);

  wire and_1_out, and_2_out, and_3_out, and_4_out, and_5_out, and_6_out, and_7_out, not_1_out, not_2_out,
       not_3_out;

  not not_1 (not_1_out, b2);
  not not_2 (not_2_out, b1);
  not not_3 (not_3_out, b0);
  and and_1 (and_1_out, b1, b0);
  and and_2 (and_2_out, b2, b0);
  and and_3 (and_3_out, b2, b1);
  and and_4 (and_4_out, not_1_out, not_2_out, b0);
  and and_5 (and_5_out, not_1_out, b1, not_3_out);
  and and_6 (and_6_out, b2, not_2_out, not_3_out);
  and and_7 (and_7_out, b2, b1, b0);
  or or_1 (s1, and_1_out, and_2_out, and_3_out);
  or or_2 (s0, and_4_out, and_5_out, and_6_out, and_7_out);
endmodule
