// Logisim project HW_4.circ as structural Verilog: 3 circuits, main circuit main
module main (
  input  r0,
  input  L,
  input  r1,
  input  r2,
  output [2:0] Q
);

  wire clk_out, d_ff_1_qn, d_ff_2_qn, d_ff_3_qn, multiplexer_1_out, multiplexer_2_out, multiplexer_3_out,
       xor_1_out;

  D_Flip_Flop d_ff_1 (.D(multiplexer_1_out), .clk(clk_out), .Q(Q[0]), .Qn(d_ff_1_qn));  // open: preset, reset
  Multiplexer multiplexer_1 (.in0(Q[2]), .in1(r0), .out(multiplexer_1_out), .sel(L));
  Clock clk (.out(clk_out));
  // NoConnect on d_ff_1_qn
  D_Flip_Flop d_ff_2 (.D(multiplexer_2_out), .clk(clk_out), .Q(Q[1]), .Qn(d_ff_2_qn));  // open: preset, reset
  Multiplexer multiplexer_2 (.in0(xor_1_out), .in1(r1), .out(multiplexer_2_out), .sel(L));
  xor xor_1 (xor_1_out, Q[2], Q[0]);
  Multiplexer multiplexer_3 (.in0(Q[1]), .in1(r2), .out(multiplexer_3_out), .sel(L));
  // NoConnect on d_ff_2_qn
  D_Flip_Flop d_ff_3 (.D(multiplexer_3_out), .clk(clk_out), .Q(Q[2]), .Qn(d_ff_3_qn));  // open: preset, reset
  // NoConnect on d_ff_3_qn
endmodule

module Q528 (
  input  r0,
  input  L,
  input  r1,
  input  r2,
  output [2:0] Q
);

  wire clk_out, d_ff_1_qn, d_ff_2_qn, d_ff_3_qn, multiplexer_1_out, multiplexer_2_out, multiplexer_3_out,
       xor_1_out;

  D_Flip_Flop d_ff_1 (.D(multiplexer_1_out), .clk(clk_out), .Q(Q[0]), .Qn(d_ff_1_qn));  // open: preset, reset
  Multiplexer multiplexer_1 (.in0(Q[2]), .in1(r0), .out(multiplexer_1_out), .sel(L));
  Clock clk (.out(clk_out));
  // NoConnect on d_ff_1_qn
  D_Flip_Flop d_ff_2 (.D(multiplexer_2_out), .clk(clk_out), .Q(Q[1]), .Qn(d_ff_2_qn));  // open: preset, reset
  Multiplexer multiplexer_2 (.in0(xor_1_out), .in1(r1), .out(multiplexer_2_out), .sel(L));
  xor xor_1 (xor_1_out, Q[2], Q[0]);
  Multiplexer multiplexer_3 (.in0(Q[1]), .in1(r2), .out(multiplexer_3_out), .sel(L));
  // NoConnect on d_ff_2_qn
  D_Flip_Flop d_ff_3 (.D(multiplexer_3_out), .clk(clk_out), .Q(Q[2]), .Qn(d_ff_3_qn));  // open: preset, reset
  // NoConnect on d_ff_3_qn
endmodule

module Q530 (
  input  r0,
  input  L,
  input  r1,
  input  r2,
  output [2:0] Q
);

  wire clk_out, d_ff_1_qn, d_ff_2_qn, d_ff_3_qn, multiplexer_1_out, multiplexer_2_out, multiplexer_3_out,
       xor_1_out;

  Multiplexer multiplexer_1 (.in0(multiplexer_3_out), .in1(r0), .out(multiplexer_1_out), .sel(L));
  Clock clk (.out(clk_out));
  D_Flip_Flop d_ff_1 (.D(multiplexer_1_out), .clk(clk_out), .Q(Q[0]), .Qn(d_ff_1_qn));  // open: preset, reset
  // NoConnect on d_ff_1_qn
  D_Flip_Flop d_ff_2 (.D(multiplexer_2_out), .clk(clk_out), .Q(Q[1]), .Qn(d_ff_2_qn));  // open: preset, reset
  Multiplexer multiplexer_2 (.in0(xor_1_out), .in1(r1), .out(multiplexer_2_out), .sel(L));
  xor xor_1 (xor_1_out, multiplexer_3_out, multiplexer_1_out);
  // NoConnect on d_ff_2_qn
  D_Flip_Flop d_ff_3 (.D(multiplexer_3_out), .clk(clk_out), .Q(Q[2]), .Qn(d_ff_3_qn));  // open: preset, reset
  Multiplexer multiplexer_3 (.in0(multiplexer_2_out), .in1(r2), .out(multiplexer_3_out), .sel(L));
  // NoConnect on d_ff_3_qn
endmodule
