// Logisim project Part_1.circ as structural Verilog: 2 circuits, main circuit Segment_7_Decoder
module main (
  input  SW3,
  input  SW2,
  input  SW1,
  input  SW0
);

  wire [6:0] segment_7_decoder_1_mout;

  Segment_7_Decoder segment_7_decoder_1 (.m3(SW3), .m2(SW2), .m1(SW1), .m0(SW0), .mout(segment_7_decoder_1_mout));
  _7_Segment_Display #(.active("false"), .decimalPoint("false")) HEX1 (
    .g(segment_7_decoder_1_mout[0]), .f(segment_7_decoder_1_mout[1]), .a(segment_7_decoder_1_mout[6]),
    .b(segment_7_decoder_1_mout[5]), .e(segment_7_decoder_1_mout[2]), .d(segment_7_decoder_1_mout[3]),
    .c(segment_7_decoder_1_mout[4]));
endmodule

module Segment_7_Decoder (
  input  m3,
  input  m2,
  input  m1,
  input  m0,
  output [6:0] mout
);

  wire and_1_out, and_2_out, and_3_out, and_4_out, and_5_out, and_6_out, and_7_out, and_8_out, and_9_out,
       and_10_out, and_11_out, and_12_out, and_13_out, and_14_out, and_15_out, and_16_out, and_17_out,
       and_18_out, and_19_out, and_20_out, and_21_out, and_22_out, and_23_out, and_24_out, not_1_out,
       not_2_out, not_3_out, not_4_out;

  not not_1 (not_1_out, m3);
  not not_2 (not_2_out, m2);
  not not_3 (not_3_out, m1);
  not not_4 (not_4_out, m0);
  and and_1 (and_1_out, not_1_out, not_2_out, not_3_out, m0);
  and and_2 (and_2_out, not_1_out, m2, not_3_out, not_4_out);
  and and_3 (and_3_out, m3, not_2_out, m1, m0);
  and and_4 (and_4_out, m3, m2, m1, not_4_out);
  and and_5 (and_5_out, not_1_out, m2, not_3_out, m0);
  and and_6 (and_6_out, not_1_out, m2, m1, not_4_out);
  and and_7 (and_7_out, m3, m2, m1, m0);
  and and_8 (and_8_out, not_1_out, not_2_out, m1, not_4_out);
  and and_9 (and_9_out, m3, m2, not_3_out, not_4_out);
  and and_10 (and_10_out, not_2_out, not_3_out, m0);
  and and_11 (and_11_out, not_1_out, m2, not_3_out, not_4_out);
  and and_12 (and_12_out, not_1_out, m2, m1, m0);
  and and_13 (and_13_out, m3, not_2_out, m0);
  and and_14 (and_14_out, m3, m2, m1, not_4_out);
  and and_15 (and_15_out, not_1_out, m2, not_3_out);
  and and_16 (and_16_out, m3, m2, m1);
  and and_17 (and_17_out, not_1_out, not_2_out, m0);
  and and_18 (and_18_out, not_1_out, not_2_out, m1);
  and and_19 (and_19_out, not_1_out, m1, m0);
  and and_20 (and_20_out, not_2_out, m1, m0);
  and and_21 (and_21_out, m3, m2, not_3_out);
  and and_22 (and_22_out, not_1_out, not_2_out, not_3_out);
  and and_23 (and_23_out, not_1_out, m2, m1, m0);
  and and_24 (and_24_out, m3, not_2_out, m1);
  or or_1 (mout[6], and_1_out, and_2_out, and_3_out, and_4_out);
  or or_2 (mout[5], and_5_out, and_6_out, and_7_out);
  or or_3 (mout[4], and_8_out, and_9_out);
  or or_4 (mout[3], and_10_out, and_11_out, and_12_out, and_13_out, and_14_out);
  or or_5 (mout[2], m0, and_15_out, and_16_out);
  or or_6 (mout[1], and_17_out, and_18_out, and_19_out, and_20_out, and_21_out);
  or or_7 (mout[0], and_22_out, and_23_out, and_24_out);
endmodule
