// Logisim project Part_3.circ as structural Verilog: 2 circuits, main circuit main
module main (
  input  C_i,
  input  [3:0] A,
  input  [3:0] B,
  output [3:0] S,
  output C_O
);

  wire FA_0_c_o, FA_1_c_o, FA_2_c_o;

  full_adder FA_0 (.c_i(C_i), .a(A[0]), .b(B[0]), .s(S[0]), .c_o(FA_0_c_o));
  full_adder FA_1 (.c_i(FA_0_c_o), .a(A[1]), .b(B[1]), .s(S[1]), .c_o(FA_1_c_o));
  full_adder FA_2 (.c_i(FA_1_c_o), .a(A[2]), .b(B[2]), .s(S[2]), .c_o(FA_2_c_o));
  full_adder FA_3 (.c_i(FA_2_c_o), .a(A[3]), .b(B[3]), .s(S[3]), .c_o(C_O));
endmodule

module full_adder (
  input  c_i,
  input  a,
  input  b,
  output s,
  output c_o
);

  wire xor_1_out;

  xor xor_1 (xor_1_out, a, b);
  Multiplexer multiplexer_1 (.in0(b), .in1(c_i), .out(c_o), .sel(xor_1_out));
  xor xor_2 (s, c_i, xor_1_out);
endmodule
