// Logisim project Part_4.circ as structural Verilog: 6 circuits, main circuit bcd_adder
module bcd_adder (
  input  C_in,
  input  [3:0] A,
  input  [3:0] B,
  output out_4,
  output out_5
);

  wire adder0_c_o, comp0_z, g0, g1, g2, g3, g4, g5, g6, s0, s1, s2, s3, s4, s5, s6;
  wire [3:0] adder0_s, adder1_s, mux0_f;

  adder_4bit adder0 (.C_i(C_in), .A(A), .B(B), .S(adder0_s), .C_O(adder0_c_o));
  adder_4bit adder1 (.C_i(1'b0), .A(adder0_s), .B(4'b0110), .S(adder1_s));  // open: C_O
  bcd_comperator comp0 (
    .b2(adder0_s[2]), .b0(adder0_s[0]), .b3(adder0_s[3]), .b1(adder0_s[1]), .b4(adder0_c_o), .z(comp0_z));
  mux_4bit_2_1 mux0 (.S(comp0_z), .A(adder0_s), .B(adder1_s), .F(mux0_f));
  Pull_Resistor pull_resistor_1 (.node(comp0_z));
  Seg7_Decoder seg0 (
    .i_m3(mux0_f[3]), .i_m2(mux0_f[2]), .i_m1(mux0_f[1]), .i_m0(mux0_f[0]),
    .o_seg({out_4, s6, s5, s4, s3, s2, s1, s0}));
  Seg7_Decoder seg1 (
    .i_m3(1'b0), .i_m2(1'b0), .i_m1(1'b0), .i_m0(comp0_z), .o_seg({out_5, g6, g5, g4, g3, g2, g1, g0}));
  _7_Segment_Display #(.active("false")) u_7_segment_display_1 (
    .g(g6), .f(g5), .a(g0), .b(g1), .e(g4), .d(g3), .c(g2), .dp(1'b1));
  _7_Segment_Display #(.active("false")) L_7_Segment_Display_2 (
    .g(s6), .f(s5), .a(s0), .b(s1), .e(s4), .d(s3), .c(s2), .dp(1'b1));
endmodule

module adder_4bit (
  input  C_i,
  input  [3:0] A,
  input  [3:0] B,
  output [3:0] S,
  output C_O
);

  wire FA_0_c_o, FA_1_c_o, FA_2_c_o;

  full_adder FA_0 (.c_i(C_i), .a(A[0]), .b(B[0]), .s(S[0]), .c_o(FA_0_c_o));
  full_adder FA_1 (.c_i(FA_0_c_o), .a(A[1]), .b(B[1]), .s(S[1]), .c_o(FA_1_c_o));
  full_adder FA_2 (.c_i(FA_1_c_o), .a(A[2]), .b(B[2]), .s(S[2]), .c_o(FA_2_c_o));
  full_adder FA_3 (.c_i(FA_2_c_o), .a(A[3]), .b(B[3]), .s(S[3]), .c_o(C_O));
endmodule

module full_adder (
  input  c_i,
  input  a,
  input  b,
  output s,
  output c_o
);

  wire xor_1_out;

  xor xor_1 (xor_1_out, a, b);
  Multiplexer multiplexer_1 (.in0(b), .in1(c_i), .out(c_o), .sel(xor_1_out));
  xor xor_2 (s, c_i, xor_1_out);
endmodule

module Seg7_Decoder (
  input  i_m3,
  input  i_m2,
  input  i_m1,
  input  i_m0,
  output [7:0] o_seg
);

  wire and_1_out, and_2_out, and_3_out, and_4_out, and_5_out, and_6_out, and_7_out, and_8_out, and_10_out,
       and_11_out, and_12_out, and_13_out, not_1_out, not_2_out, not_3_out, not_4_out;

  not not_1 (not_1_out, i_m3);
  not not_2 (not_2_out, i_m2);
  not not_3 (not_3_out, i_m1);
  not not_4 (not_4_out, i_m0);
  and and_1 (and_1_out, not_1_out, not_2_out, not_3_out);
  and and_2 (and_2_out, i_m2, i_m1, i_m0);
  and and_3 (and_3_out, not_1_out, not_2_out, i_m0);
  and and_4 (and_4_out, not_2_out, i_m1);
  and and_5 (and_5_out, i_m2, not_3_out);
  and and_6 (and_6_out, not_1_out, not_2_out, not_3_out, i_m0);
  and and_7 (and_7_out, i_m2, not_3_out, not_4_out);
  and and_8 (and_8_out, i_m2, i_m1, i_m0);
  and and_9 (o_seg[2], not_2_out, i_m1, not_4_out);
  and and_10 (and_10_out, i_m2, not_3_out, i_m0);
  and and_11 (and_11_out, i_m2, i_m1, not_4_out);
  and and_12 (and_12_out, not_1_out, not_2_out, not_3_out, i_m0);
  and and_13 (and_13_out, i_m2, not_3_out, not_4_out);
  or or_1 (o_seg[6], and_1_out, and_2_out);
  or or_2 (o_seg[5], and_3_out, and_4_out);
  or or_3 (o_seg[4], i_m0, and_5_out);
  or or_4 (o_seg[3], and_6_out, and_7_out, and_8_out);
  or or_5 (o_seg[1], and_10_out, and_11_out);
  or or_6 (o_seg[0], and_12_out, and_13_out);

  assign o_seg[7] = 1'b1;
endmodule

module bcd_comperator (
  input  b2,
  input  b0,
  input  b3,
  input  b1,
  input  b4,
  output z
);

  wire and_1_out, and_2_out;

  and and_1 (and_1_out, b2, b3);
  and and_2 (and_2_out, b3, b1);
  or or_1 (z, and_1_out, and_2_out, b4);
endmodule

module mux_4bit_2_1 (
  input  S,
  input  [3:0] A,
  input  [3:0] B,
  output [3:0] F
);

  Multiplexer multiplexer_1 (.in0(A[0]), .in1(B[0]), .out(F[0]), .sel(S));
  Multiplexer multiplexer_2 (.in0(A[1]), .in1(B[1]), .out(F[1]), .sel(S));
  Multiplexer multiplexer_3 (.in0(A[2]), .in1(B[2]), .out(F[2]), .sel(S));
  Multiplexer multiplexer_4 (.in0(A[3]), .in1(B[3]), .out(F[3]), .sel(S));
endmodule
