// Logisim project Part_5.circ as structural Verilog: 2 circuits, main circuit main
module main (
  input  C_in,
  input  [3:0] A,
  input  [3:0] B,
  input  [3:0] C,
  input  [3:0] D,
  output out_6,
  output out_7,
  output out_8
);

  wire BCD_0_c_out, pull_resistor_1_node;
  wire [6:0] BCD_0_seg7_out, BCD_1_seg7_out, seg1_o_seg;

  Pull_Resistor pull_resistor_1 (.node(pull_resistor_1_node));
  bcd_4bit_adder BCD_0 (.C_in(C_in), .A(A), .B(B), .seg7_out({out_6, BCD_0_seg7_out}), .C_out(BCD_0_c_out));
  bcd_4bit_adder BCD_1 (
    .C_in(BCD_0_c_out), .A(C), .B(D), .seg7_out({out_7, BCD_1_seg7_out}), .C_out(pull_resistor_1_node));
  Seg7_Decoder seg1 (.i_m3(1'b0), .i_m2(1'b0), .i_m1(1'b0), .i_m0(pull_resistor_1_node), .o_seg({out_8, seg1_o_seg}));
  _7_Segment_Display #(.active("false")) L_7_Segment_Display_2 (
    .g(BCD_0_seg7_out[6]), .f(BCD_0_seg7_out[5]), .a(BCD_0_seg7_out[0]), .b(BCD_0_seg7_out[1]),
    .e(BCD_0_seg7_out[4]), .d(BCD_0_seg7_out[3]), .c(BCD_0_seg7_out[2]), .dp(1'b1));
  _7_Segment_Display #(.active("false")) u_7_segment_display_1 (
    .g(BCD_1_seg7_out[6]), .f(BCD_1_seg7_out[5]), .a(BCD_1_seg7_out[0]), .b(BCD_1_seg7_out[1]),
    .e(BCD_1_seg7_out[4]), .d(BCD_1_seg7_out[3]), .c(BCD_1_seg7_out[2]), .dp(1'b1));
  _7_Segment_Display #(.active("false")) u_7_segment_display_2 (
    .g(seg1_o_seg[6]), .f(seg1_o_seg[5]), .a(seg1_o_seg[0]), .b(seg1_o_seg[1]), .e(seg1_o_seg[4]),
    .d(seg1_o_seg[3]), .c(seg1_o_seg[2]), .dp(1'b1));
endmodule

module bcd_4bit_adder (
  input  C_in,
  input  [3:0] A,
  input  [3:0] B,
  output [7:0] seg7_out,
  output C_out
);

  wire adder0_c_o;
  wire [3:0] adder0_s, adder1_s, mux0_f;

  adder_4bit adder0 (.C_i(C_in), .A(A), .B(B), .S(adder0_s), .C_O(adder0_c_o));
  adder_4bit adder1 (.C_i(1'b0), .A(adder0_s), .B(4'b0110), .S(adder1_s));  // open: C_O
  bcd_comperator comp0 (
    .b2(adder0_s[2]), .b0(adder0_s[0]), .b3(adder0_s[3]), .b1(adder0_s[1]), .b4(adder0_c_o), .z(C_out));
  Pull_Resistor pull_resistor_1 (.node(C_out));
  mux_4bit_2_1 mux0 (.S(C_out), .A(adder0_s), .B(adder1_s), .F(mux0_f));
  Seg7_Decoder seg0 (.i_m3(mux0_f[3]), .i_m2(mux0_f[2]), .i_m1(mux0_f[1]), .i_m0(mux0_f[0]), .o_seg(seg7_out));
endmodule
