// Logisim project Part_7.circ as structural Verilog: 2 circuits, main circuit Part_7
module Part_7 (
  input  [5:0] B
);

  wire [6:0] mother_of_all_combinational_circuits_1_seg0, mother_of_all_combinational_circuits_1_seg1;

  mother_of_all_combinational_circuits mother_of_all_combinational_circuits_1 (
    .b(B), .seg1(mother_of_all_combinational_circuits_1_seg1),
    .seg0(mother_of_all_combinational_circuits_1_seg0));
  _7_Segment_Display #(.active("false")) u_7_segment_display_1 (
    .g(mother_of_all_combinational_circuits_1_seg1[6]), .f(mother_of_all_combinational_circuits_1_seg1[5]),
    .a(mother_of_all_combinational_circuits_1_seg1[0]), .b(mother_of_all_combinational_circuits_1_seg1[1]),
    .e(mother_of_all_combinational_circuits_1_seg1[4]), .d(mother_of_all_combinational_circuits_1_seg1[3]),
    .c(mother_of_all_combinational_circuits_1_seg1[2]), .dp(1'b1));
  _7_Segment_Display #(.active("false")) u_7_segment_display_2 (
    .g(mother_of_all_combinational_circuits_1_seg0[6]), .f(mother_of_all_combinational_circuits_1_seg0[5]),
    .a(mother_of_all_combinational_circuits_1_seg0[0]), .b(mother_of_all_combinational_circuits_1_seg0[1]),
    .e(mother_of_all_combinational_circuits_1_seg0[4]), .d(mother_of_all_combinational_circuits_1_seg0[3]),
    .c(mother_of_all_combinational_circuits_1_seg0[2]), .dp(1'b1));
endmodule

module mother_of_all_combinational_circuits (
  input  [5:0] b,
  output [6:0] seg1,
  output [6:0] seg0
);

  wire and_1_out, and_2_out, and_3_out, and_4_out, and_5_out, and_6_out, and_7_out, and_8_out, and_9_out,
       and_10_out, and_11_out, and_12_out, and_13_out, and_14_out, and_15_out, and_16_out, and_17_out,
       and_18_out, and_19_out, and_20_out, and_21_out, and_22_out, and_23_out, and_24_out, and_25_out,
       and_26_out, and_27_out, and_28_out, and_29_out, and_30_out, and_31_out, and_32_out, and_33_out,
       and_34_out, and_35_out, and_36_out, and_37_out, and_38_out, and_39_out, and_40_out, and_41_out,
       and_42_out, and_43_out, and_44_out, and_45_out, and_46_out, and_47_out, and_48_out, and_49_out,
       and_50_out, and_51_out, and_52_out, and_53_out, and_54_out, and_55_out, and_56_out, and_57_out,
       and_58_out, and_59_out, and_60_out, and_61_out, and_62_out, and_63_out, and_64_out, and_65_out,
       and_66_out, and_67_out, and_68_out, and_69_out, and_70_out, and_71_out, and_72_out, and_73_out,
       and_74_out, and_75_out, and_76_out, and_77_out, and_78_out, and_79_out, and_80_out, and_81_out,
       and_82_out, and_83_out, and_84_out, and_85_out, and_86_out, and_87_out, and_88_out, and_89_out,
       and_90_out, and_91_out, and_92_out, and_93_out, and_94_out, and_95_out, and_96_out, and_97_out,
       and_98_out, and_99_out, and_100_out, and_101_out, and_102_out, and_103_out, and_104_out, and_105_out,
       and_106_out, and_107_out, and_108_out, and_109_out, and_110_out, and_111_out, and_112_out,
       and_113_out, and_114_out, and_115_out, and_116_out, and_117_out, and_118_out, and_119_out,
       and_120_out, and_121_out, and_122_out, and_123_out, and_124_out, and_125_out, and_126_out, not_1_out,
       not_2_out, not_3_out, not_4_out, not_5_out, not_6_out;

  not not_1 (not_1_out, b[5]);
  not not_2 (not_2_out, b[4]);
  not not_3 (not_3_out, b[3]);
  not not_4 (not_4_out, b[2]);
  not not_5 (not_5_out, b[1]);
  not not_6 (not_6_out, b[0]);
  and and_1 (and_1_out, not_1_out, not_2_out);
  and and_2 (and_2_out, not_1_out, not_3_out, not_4_out);
  and and_3 (and_3_out, b[5], not_2_out, not_3_out);
  and and_4 (and_4_out, not_1_out, b[4], b[2]);
  and and_5 (and_5_out, not_1_out, b[4], b[3]);
  and and_6 (and_6_out, not_1_out, b[4], b[3], b[2], b[1]);
  and and_7 (and_7_out, b[5], not_2_out);
  and and_8 (and_8_out, b[5], not_3_out);
  and and_9 (and_9_out, b[5], not_4_out);
  and and_10 (and_10_out, b[5], not_2_out, b[3]);
  and and_11 (and_11_out, not_2_out, b[3], b[1]);
  and and_12 (and_12_out, not_2_out, b[3], b[2]);
  and and_13 (and_13_out, b[4], not_3_out, not_4_out, not_5_out);
  and and_14 (and_14_out, not_1_out, b[4], not_3_out, not_4_out);
  and and_15 (and_15_out, not_1_out, b[4], not_3_out);
  and and_16 (and_16_out, not_1_out, b[4], not_4_out);
  and and_17 (and_17_out, not_1_out, b[3], b[2], not_5_out);
  and and_18 (and_18_out, not_1_out, not_2_out, b[3], b[1]);
  and and_19 (and_19_out, not_1_out, not_2_out, b[3], b[1]);
  and and_20 (and_20_out, not_1_out, not_2_out, b[3], b[2]);
  and and_21 (and_21_out, not_1_out, b[4], not_3_out, not_4_out);
  and and_22 (and_22_out, b[5], b[4], b[2]);
  and and_23 (and_23_out, b[5], b[4], b[3]);
  and and_24 (and_24_out, b[5], b[4], b[1]);
  and and_25 (and_25_out, b[5], not_2_out, b[3]);
  and and_26 (and_26_out, not_2_out, b[3], b[1]);
  and and_27 (and_27_out, not_2_out, b[3], b[2]);
  and and_28 (and_28_out, b[4], not_3_out, not_4_out, not_5_out);
  and and_29 (and_29_out, not_1_out, b[4], not_3_out, not_4_out);
  and and_30 (and_30_out, not_1_out, not_2_out, not_3_out, not_4_out, not_5_out);
  and and_31 (and_31_out, b[5], not_2_out, not_3_out, b[2], not_5_out, b[0]);
  and and_32 (and_32_out, not_1_out, not_2_out, not_3_out, b[2], b[1], b[0]);
  and and_33 (and_33_out, b[5], not_2_out, b[3], not_4_out, not_5_out);
  and and_34 (and_34_out, not_1_out, not_2_out, b[3], not_4_out, b[1]);
  and and_35 (and_35_out, b[5], not_2_out, b[3], b[2], b[1], b[0]);
  and and_36 (and_36_out, b[5], b[4], not_3_out, not_4_out, b[1]);
  and and_37 (and_37_out, not_1_out, b[4], not_3_out, b[2], not_5_out);
  and and_38 (and_38_out, b[5], b[4], b[3], b[2], not_5_out);
  and and_39 (and_39_out, not_1_out, b[4], b[3], b[2], b[1]);
  and and_40 (and_40_out, not_1_out, not_3_out, not_4_out, not_5_out, b[0]);
  and and_41 (and_41_out, b[5], b[3], not_4_out, not_5_out, b[0]);
  and and_42 (and_42_out, not_1_out, b[4], b[3], b[1], b[0]);
  and and_43 (and_43_out, b[5], not_2_out, not_3_out, not_4_out, not_5_out);
  and and_44 (and_44_out, not_1_out, not_2_out, not_3_out, not_4_out, b[1]);
  and and_45 (and_45_out, b[5], not_2_out, b[3], not_4_out, b[1]);
  and and_46 (and_46_out, not_1_out, not_2_out, b[3], b[2], not_5_out);
  and and_47 (and_47_out, not_1_out, b[4], not_3_out, not_4_out, not_5_out, b[0]);
  and and_48 (and_48_out, b[5], b[4], not_3_out, b[2], not_5_out);
  and and_49 (and_49_out, not_1_out, b[4], not_3_out, b[2], b[1]);
  and and_50 (and_50_out, b[5], b[4], b[3], not_4_out, not_5_out, b[0]);
  and and_51 (and_51_out, not_1_out, b[4], b[3], not_4_out, b[1], b[0]);
  and and_52 (and_52_out, b[5], b[4], b[3], b[2], b[1]);
  and and_53 (and_53_out, b[5], not_2_out, not_3_out, not_5_out, b[0]);
  and and_54 (and_54_out, not_1_out, not_2_out, not_3_out, b[1], b[0]);
  and and_55 (and_55_out, b[5], not_2_out, b[3], b[1], b[0]);
  and and_56 (and_56_out, not_1_out, not_2_out, not_3_out, b[2], not_5_out);
  and and_57 (and_57_out, not_1_out, b[3], not_5_out, b[0]);
  and and_58 (and_58_out, not_1_out, not_2_out, b[3], b[2], b[1]);
  and and_59 (and_59_out, not_1_out, b[4], b[3], not_4_out, not_5_out);
  and and_60 (and_60_out, b[5], not_2_out, not_3_out, not_4_out, b[1]);
  and and_61 (and_61_out, b[5], not_2_out, b[3], b[2], not_5_out);
  and and_62 (and_62_out, b[5], b[4], not_3_out, b[2], b[1]);
  and and_63 (and_63_out, b[5], not_3_out, not_5_out, b[0]);
  and and_64 (and_64_out, not_1_out, not_3_out, b[1], b[0]);
  and and_65 (and_65_out, b[4], not_4_out, not_5_out, b[0]);
  and and_66 (and_66_out, b[4], b[3], not_4_out, b[0]);
  and and_67 (and_67_out, not_2_out, b[2], b[0]);
  and and_68 (and_68_out, b[5], b[3], b[1], b[0]);
  and and_69 (and_69_out, not_1_out, not_3_out, not_4_out, not_5_out, b[0]);
  and and_70 (and_70_out, b[5], not_2_out, not_3_out, not_4_out, b[1], not_6_out);
  and and_71 (and_71_out, not_1_out, not_2_out, not_3_out, b[2], not_5_out, not_6_out);
  and and_72 (and_72_out, b[5], not_2_out, not_3_out, b[2], not_5_out, b[0]);
  and and_73 (and_73_out, not_1_out, not_2_out, not_3_out, b[2], b[1], b[0]);
  and and_74 (and_74_out, b[5], b[3], not_4_out, not_5_out, b[0]);
  and and_75 (and_75_out, not_1_out, b[3], not_4_out, b[1], b[0]);
  and and_76 (and_76_out, b[5], not_2_out, b[3], b[2], not_5_out, not_6_out);
  and and_77 (and_77_out, not_1_out, not_2_out, b[3], b[2], b[1], not_6_out);
  and and_78 (and_78_out, b[5], not_2_out, b[3], b[2], b[1], b[0]);
  and and_79 (and_79_out, b[5], b[4], not_3_out, not_4_out, b[1], b[0]);
  and and_80 (and_80_out, not_1_out, b[4], not_3_out, not_5_out, b[0]);
  and and_81 (and_81_out, b[5], b[4], not_3_out, b[2], b[1], not_6_out);
  and and_82 (and_82_out, not_1_out, b[4], b[3], not_4_out, not_5_out, not_6_out);
  and and_83 (and_83_out, b[5], b[4], b[3], not_5_out, b[0]);
  and and_84 (and_84_out, not_1_out, b[4], b[3], b[1], b[0]);
  and and_85 (and_85_out, b[5], not_2_out, not_3_out, not_4_out, not_5_out, not_6_out);
  and and_86 (and_86_out, not_1_out, not_2_out, not_3_out, not_4_out, not_5_out, b[0]);
  and and_87 (and_87_out, not_1_out, not_2_out, not_3_out, not_4_out, b[1], not_6_out);
  and and_88 (and_88_out, b[5], not_2_out, b[3], not_4_out, not_5_out, b[0]);
  and and_89 (and_89_out, b[5], not_2_out, b[3], not_4_out, b[1], not_6_out);
  and and_90 (and_90_out, not_1_out, not_2_out, b[3], not_4_out, b[1], b[0]);
  and and_91 (and_91_out, not_1_out, not_2_out, b[3], b[2], not_5_out, not_6_out);
  and and_92 (and_92_out, b[5], b[4], not_3_out, not_4_out, b[1], b[0]);
  and and_93 (and_93_out, b[5], b[4], not_3_out, b[2], not_5_out, not_6_out);
  and and_94 (and_94_out, not_1_out, b[4], not_3_out, b[2], not_5_out, b[0]);
  and and_95 (and_95_out, not_1_out, b[4], not_3_out, b[2], b[1], not_6_out);
  and and_96 (and_96_out, b[5], b[4], b[3], b[2], not_5_out, b[0]);
  and and_97 (and_97_out, b[5], b[4], b[3], b[2], b[1], not_6_out);
  and and_98 (and_98_out, not_1_out, b[4], b[3], b[2], b[1], b[0]);
  and and_99 (and_99_out, not_1_out, not_2_out, not_3_out, not_5_out, b[0]);
  and and_100 (and_100_out, b[5], not_3_out, not_4_out, b[1], b[0]);
  and and_101 (and_101_out, b[5], not_2_out, not_3_out, b[2], not_5_out, not_6_out);
  and and_102 (and_102_out, not_1_out, not_2_out, not_3_out, b[2], b[1], not_6_out);
  and and_103 (and_103_out, b[5], not_2_out, b[3], not_5_out, b[0]);
  and and_104 (and_104_out, not_1_out, not_2_out, b[3], b[1], b[0]);
  and and_105 (and_105_out, b[5], not_2_out, b[3], b[2], b[1], not_6_out);
  and and_106 (and_106_out, not_1_out, b[4], not_3_out, not_4_out, not_5_out, not_6_out);
  and and_107 (and_107_out, not_1_out, not_3_out, b[2], not_5_out, b[0]);
  and and_108 (and_108_out, b[5], b[4], not_3_out, b[1], b[0]);
  and and_109 (and_109_out, b[5], b[4], b[3], not_4_out, not_5_out, not_6_out);
  and and_110 (and_110_out, not_1_out, b[4], b[3], not_4_out, not_5_out, b[0]);
  and and_111 (and_111_out, not_1_out, b[4], b[3], not_4_out, b[1], not_6_out);
  and and_112 (and_112_out, b[5], b[3], b[2], not_5_out, b[0]);
  and and_113 (and_113_out, not_1_out, b[3], b[2], b[1], b[0]);
  and and_114 (and_114_out, not_1_out, not_2_out, not_3_out, not_4_out, not_5_out, b[0]);
  and and_115 (and_115_out, b[5], not_2_out, not_3_out, not_4_out, b[1], not_6_out);
  and and_116 (and_116_out, not_1_out, not_2_out, not_3_out, b[2], not_5_out, not_6_out);
  and and_117 (and_117_out, b[5], not_2_out, b[3], not_4_out, not_5_out, b[0]);
  and and_118 (and_118_out, not_1_out, not_2_out, b[3], not_4_out, b[1], b[0]);
  and and_119 (and_119_out, b[5], not_2_out, b[3], b[2], not_5_out, not_6_out);
  and and_120 (and_120_out, not_1_out, not_2_out, b[3], b[2], b[1], not_6_out);
  and and_121 (and_121_out, b[5], b[4], not_3_out, not_4_out, b[1], b[0]);
  and and_122 (and_122_out, not_1_out, b[4], not_3_out, b[2], not_5_out, b[0]);
  and and_123 (and_123_out, b[5], b[4], not_3_out, b[2], b[1], not_6_out);
  and and_124 (and_124_out, not_1_out, b[4], b[3], not_4_out, not_5_out, not_6_out);
  and and_125 (and_125_out, b[5], b[4], b[3], b[2], not_5_out, b[0]);
  and and_126 (and_126_out, not_1_out, b[4], b[3], b[2], b[1], b[0]);
  or or_1 (seg1[6], and_1_out, and_2_out);
  or or_2 (seg1[5], and_3_out, and_4_out, and_5_out);
  or or_3 (seg1[4], and_6_out, and_7_out, and_8_out, and_9_out);
  or or_4 (seg1[3], and_10_out, and_11_out, and_12_out, and_13_out, and_14_out);
  or or_5 (seg1[2], and_15_out, and_16_out, and_17_out, and_18_out);
  or or_6 (seg1[1], and_19_out, and_20_out, and_21_out, and_22_out, and_23_out, and_24_out);
  or or_7 (seg1[0], and_25_out, and_26_out, and_27_out, and_28_out, and_29_out);
  or or_8 (seg0[6], and_30_out, and_31_out, and_32_out, and_33_out, and_34_out, and_35_out, and_36_out, and_37_out, and_38_out, and_39_out, and_40_out, and_41_out, and_42_out);
  or or_9 (seg0[5], and_43_out, and_44_out, and_45_out, and_46_out, and_47_out, and_48_out, and_49_out, and_50_out, and_51_out, and_52_out, and_53_out, and_54_out, and_55_out);
  or or_10 (seg0[4], and_56_out, and_57_out, and_58_out, and_59_out, and_60_out, and_61_out, and_62_out, and_63_out, and_64_out, and_65_out, and_66_out, and_67_out, and_68_out);
  or or_11 (seg0[3], and_69_out, and_70_out, and_71_out, and_72_out, and_73_out, and_74_out, and_75_out, and_76_out, and_77_out, and_78_out, and_79_out, and_80_out, and_81_out, and_82_out, and_83_out, and_84_out);
  or or_12 (seg0[2], and_85_out, and_86_out, and_87_out, and_88_out, and_89_out, and_90_out, and_91_out, and_92_out, and_93_out, and_94_out, and_95_out, and_96_out, and_97_out, and_98_out);
  or or_13 (seg0[1], and_99_out, and_100_out, and_101_out, and_102_out, and_103_out, and_104_out, and_105_out, and_106_out, and_107_out, and_108_out, and_109_out, and_110_out, and_111_out, and_112_out, and_113_out);
  or or_14 (seg0[0], and_114_out, and_115_out, and_116_out, and_117_out, and_118_out, and_119_out, and_120_out, and_121_out, and_122_out, and_123_out, and_124_out, and_125_out, and_126_out);
endmodule
