// Logisim project Lab_3.circ as structural Verilog
module Gated_RS_Latch (
  input  R,
  input  Clk,
  input  S,
  output Qa,
  output Qb
);

  wire R_g_out, S_g_out;

  and R_g (R_g_out, R, Clk);
  and S_g (S_g_out, Clk, S);
  nor nor_1 (Qa, R_g_out, Qb);
  nor nor_2 (Qb, Qa, S_g_out);
endmodule

module Gated_D_Latch (
  input  D,
  input  Clk,
  output Qa,
  output Qb
);

  wire nand_1_out, nand_2_out, not_1_out;

  not not_1 (not_1_out, D);
  nand nand_1 (nand_1_out, D, Clk);
  nand nand_2 (nand_2_out, Clk, not_1_out);
  nand nand_3 (Qa, nand_1_out, Qb);
  nand nand_4 (Qb, Qa, nand_2_out);
endmodule

module MS_D_FlipFlop (
  input  D,
  input  Clk,
  output Q,
  output notQ
);

  wire gated_d_latch_1_qa, gated_d_latch_1_qb, not_1_out;

  not not_1 (not_1_out, Clk);
  Gated_D_Latch gated_d_latch_1 (.D(D), .Clk(not_1_out), .Qa(gated_d_latch_1_qa), .Qb(gated_d_latch_1_qb));
  // NoConnect on gated_d_latch_1_qb
  Gated_D_Latch gated_d_latch_2 (.D(gated_d_latch_1_qa), .Clk(not_1_out), .Qa(Q), .Qb(notQ));
endmodule

module D3_Latch (
  input  D,
  input  Clk,
  output Qa,
  output Qb,
  output Qc
);

  wire Gated_D_Latch_qn, Negedge_D_Latch_qn, Posedge_D_Latch_qn;

  D_Flip_Flop #(.trigger("high")) Gated_D_Latch (
    .D(D), .clk(Clk), .Q(Qa), .Qn(Gated_D_Latch_qn));  // open: preset, reset
  D_Flip_Flop Posedge_D_Latch (.D(D), .clk(Clk), .Q(Qb), .Qn(Posedge_D_Latch_qn));  // open: preset, reset
  D_Flip_Flop #(.trigger("falling")) Negedge_D_Latch (
    .D(D), .clk(Clk), .Q(Qc), .Qn(Negedge_D_Latch_qn));  // open: preset, reset
  // NoConnect on Gated_D_Latch_qn
  // NoConnect on Posedge_D_Latch_qn
  // NoConnect on Negedge_D_Latch_qn
endmodule

module Input_4Bit_Latch (
  input  En,
  input  A,
  input  B,
  input  C,
  input  D,
  output [3:0] F
);

  wire d_ff_1_qn, d_ff_2_qn, d_ff_3_qn, d_ff_4_qn;

  D_Flip_Flop #(.trigger("high")) d_ff_1 (.D(A), .clk(En), .Q(F[0]), .Qn(d_ff_1_qn));  // open: preset, reset
  D_Flip_Flop #(.trigger("high")) d_ff_2 (.D(B), .clk(En), .Q(F[1]), .Qn(d_ff_2_qn));  // open: preset, reset
  D_Flip_Flop #(.trigger("high")) d_ff_3 (.D(C), .clk(En), .Q(F[2]), .Qn(d_ff_3_qn));  // open: preset, reset
  D_Flip_Flop #(.trigger("high")) d_ff_4 (.D(D), .clk(En), .Q(F[3]), .Qn(d_ff_4_qn));  // open: preset, reset
  // NoConnect on d_ff_1_qn
  // NoConnect on d_ff_2_qn
  // NoConnect on d_ff_3_qn
  // NoConnect on d_ff_4_qn
endmodule

module Part_5 (
  input  En,
  input  [3:0] HEX0,
  input  [3:0] HEX1,
  input  [3:0] HEX2,
  input  [3:0] HEX3
);

  wire not_1_out;
  wire [3:0] input_4bit_latch_1_f, input_4bit_latch_2_f, input_4bit_latch_3_f, input_4bit_latch_4_f;

  not not_1 (not_1_out, En);
  Input_4Bit_Latch input_4bit_latch_1 (
    .A(HEX0[0]), .B(HEX0[1]), .C(HEX0[2]), .D(HEX0[3]), .En(not_1_out), .F(input_4bit_latch_1_f));
  Input_4Bit_Latch input_4bit_latch_2 (
    .A(HEX1[0]), .B(HEX1[1]), .C(HEX1[2]), .D(HEX1[3]), .En(not_1_out), .F(input_4bit_latch_2_f));
  Input_4Bit_Latch input_4bit_latch_3 (
    .A(HEX2[0]), .B(HEX2[1]), .C(HEX2[2]), .D(HEX2[3]), .En(En), .F(input_4bit_latch_3_f));
  Input_4Bit_Latch input_4bit_latch_4 (
    .A(HEX3[0]), .B(HEX3[1]), .C(HEX3[2]), .D(HEX3[3]), .En(En), .F(input_4bit_latch_4_f));
  Hex_Digit_Display hex_digit_display_1 (.value(input_4bit_latch_1_f));  // open: dp
  Hex_Digit_Display hex_digit_display_2 (.value(input_4bit_latch_2_f));  // open: dp
  Hex_Digit_Display hex_digit_display_3 (.value(input_4bit_latch_3_f));  // open: dp
  Hex_Digit_Display hex_digit_display_4 (.value(input_4bit_latch_4_f));  // open: dp
endmodule
