// Logisim project Lab_4.circ as structural Verilog: 3 circuits, main circuit main
module main (
  input  in_1,
  output out_2
);

  wire clock_1_out;

  Clock clock_1 (.out(clock_1_out));
  T_FlipFlop t_flipflop_1 (.T(in_1), .Clk(clock_1_out), .Q(out_2));  // open: Clr
endmodule

module T_FlipFlop (
  input  T,
  input  Clk,
  input  Clr,
  output Q
);

  wire t_ff_1_qn;

  T_Flip_Flop t_ff_1 (.T(T), .clk(Clk), .Q(Q), .Qn(t_ff_1_qn), .reset(Clr));  // open: preset
  // NoConnect on t_ff_1_qn
endmodule

module T_FlipFlop_8Bits (
  input  T,
  input  Clk,
  input  Clr,
  output [7:0] Qt
);

  wire and_1_out, and_2_out, and_3_out, and_4_out, and_5_out, and_6_out, and_7_out;

  T_FlipFlop t_flipflop_1 (.T(T), .Clk(Clk), .Clr(Clr), .Q(Qt[0]));
  T_FlipFlop t_flipflop_2 (.T(and_7_out), .Clk(Clk), .Clr(Clr), .Q(Qt[4]));
  and and_1 (and_1_out, T, Qt[0]);
  and and_2 (and_2_out, and_7_out, Qt[4]);
  T_FlipFlop t_flipflop_3 (.T(and_1_out), .Clk(Clk), .Clr(Clr), .Q(Qt[1]));
  T_FlipFlop t_flipflop_4 (.T(and_2_out), .Clk(Clk), .Clr(Clr), .Q(Qt[5]));
  and and_3 (and_3_out, and_1_out, Qt[1]);
  and and_4 (and_4_out, and_2_out, Qt[5]);
  T_FlipFlop t_flipflop_5 (.T(and_3_out), .Clk(Clk), .Clr(Clr), .Q(Qt[2]));
  T_FlipFlop t_flipflop_6 (.T(and_4_out), .Clk(Clk), .Clr(Clr), .Q(Qt[6]));
  and and_5 (and_5_out, and_3_out, Qt[2]);
  and and_6 (and_6_out, and_4_out, Qt[6]);
  T_FlipFlop t_flipflop_7 (.T(and_5_out), .Clk(Clk), .Clr(Clr), .Q(Qt[3]));
  T_FlipFlop t_flipflop_8 (.T(and_6_out), .Clk(Clk), .Clr(Clr), .Q(Qt[7]));
  and and_7 (and_7_out, and_5_out, Qt[3]);

  // Other names for the same wires on the sheet: Q0 = Qt[0]; Q1 = Qt[1]; Q2 = Qt[2]; Q3 = Qt[3]; Q4 = Qt[4];
  //   Q5 = Qt[5]; Q6 = Qt[6]; Q7 = Qt[7]
endmodule
